# Fritzing sketch TempSensor (saved by Fritzing 0.9.2b)
breadboards: 1

parts:
  DS1 = DS18B20 1-Wire Temperature Sensor Probe Cable
  LED1 = LED - 5mm [color="Orange (612nm)" package="5 mm [THT]"]
  R1 = Resistor [tolerance=±5% resistance=220 package=THT]
  J1 = T Cobbler Plus
  LED2 = LED - 5mm [color="Blue (505nm)" package="5 mm [THT]"]
  R2 = Resistor [tolerance=±5% resistance=220 package=THT]
  R3 = Resistor [tolerance=±5% resistance=4.7k package=THT]

nets:
  N1: DS1.GND, LED1.anode, J1.SCL
  VDD: DS1.VDD, J1.3V3, R3.Pin_1
  N2: DS1.shield, J1.5.0V#3, R3.Pin_0
  N3: LED1.cathode, R1.Pin_1
  N4: R1.Pin_0, J1.#23
  N5: J1.#21, R2.Pin_0
  N6: LED2.cathode, R2.Pin_1

notes:
  secondary LED: Pin 21
  DS18B20 Temperature Sensor: Pin 4
  Status LED: Pin 6

custom parts:
  T Cobbler Plus: The T-Cobbler Plus is an add on prototyping board from Adafruit specifically designed for the Raspberry Pi B+ that can break out all those tasty power, GPIO, I2C and SPI pins from the 40-pin header onto a solderless breadboard. This set will make "cobbling together" prototypes with the Pi super easy. The T-Cobbler Plus can plug into any solderless breadboard.
